# Fritzing sketch BooleanLogic (saved by Fritzing 0.9.2b)
breadboards: 1

parts:
  S1 = Pushbutton [package="[THT]"]
  S2 = Pushbutton [package="[THT]"]
  S3 = Pushbutton [package="[THT]"]
  LED1 = LED - 5mm [color="Green (555nm)" package="5 mm [THT]"]
  LED2 = LED - 5mm [color="Green (555nm)" package="5 mm [THT]"]
  LED3 = LED - 5mm [color="Green (555nm)" package="5 mm [THT]"]
  LED4 = LED - 5mm [color="Red (633nm)" package="5 mm [THT]"]
  R1 = Resistor [tolerance=±5% resistance=1k package=THT]
  R2 = Resistor [tolerance=±5% resistance=1k package=THT]
  R3 = Resistor [tolerance=±5% resistance=1k package=THT]
  R4 = Resistor [tolerance=±5% resistance=1k package=THT]
  R5 = Resistor [tolerance=±5% resistance=1k package=THT]
  R6 = Resistor [tolerance=±5% resistance=1k package=THT]
  R7 = Resistor [tolerance=±5% resistance=1k package=THT]
  Part1 = Arduino Uno (Rev3)

nets:
  N1: S1.Pin_1, S1.Pin_2, R7.Pin_0, Part1.D2
  N2: S1.Pin_3, S1.Pin_4, S2.Pin_3, S2.Pin_4, S3.Pin_3, S3.Pin_4, Part1.5V
  N3: S2.Pin_1, S2.Pin_2, R3.Pin_0, Part1.D11_PWM/MOSI
  N4: S3.Pin_1, S3.Pin_2, R2.Pin_0, Part1.D12/MISO
  N5: LED1.cathode, R6.Pin_0
  N6: LED1.anode, Part1.D3_PWM
  N7: LED2.cathode, R5.Pin_0
  N8: LED2.anode, Part1.D4
  N9: LED3.cathode, R4.Pin_0
  N10: LED3.anode, Part1.D5_PWM
  N11: LED4.cathode, R1.Pin_0
  N12: LED4.anode, Part1.D13/SCK
  N13: R1.Pin_1, R2.Pin_1, R3.Pin_1, R4.Pin_1, R5.Pin_1, R6.Pin_1, R7.Pin_1, Part1.GND
