# Fritzing sketch DataCollect-1 (saved by Fritzing 0.9.3b)
breadboards: 1

parts:
  part = Adafruit BME280
  part_2 = Adafruit MicroSD card breakout board [part_number="Adafruit #254"]
  part_3 = Arduino Uno (Rev3)

nets:
  VIN: part.VIN, part_3.5V
  GND: part.GND, part_2.GND, part_3.GND
  N1: part.SCK/SCL, part_2.CLK, part_3.D13/SCK
  N2: part.SDO/ADR, part_2.DO, part_3.D12/MISO
  N3: part.SDI/SDA, part_2.DI, part_3.D11_PWM/MOSI
  N4: part.CS, part_3.D10_PWM/SS
  +3V3: part_2.+3V3, part_3.3V3
  N5: part_2.CS, part_3.D9_PWM

custom parts:
  Adafruit BME280: Bosch has stepped up their game with their new BME280 sensor, an environmental sensor with temperature, barometric pressure and humidity! This sensor is great for all sorts of weather/environmental sensing and can even be used in both I2C and SPI! This precision sensor from Bosch is the best low-cost sensing solution for measuring humidity with ±3% accuracy, barometric pressure with ±1 hPa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
  Adafruit MicroSD card breakout board: Not just a simple breakout board, this microSD adapter goes the extra mile - designed for ease of use. Onboard 5v->3v regulator provides 150mA for power-hungry cards 3v level shifting means you can use this with ease on either 3v or 5v systems Uses a proper level shifting chip, not resistors: less problems, and faster read/write access Use 3 or 4 digital pins to read and write 2Gb+ of storage!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
