# Fritzing sketch Ard-InfraRed (saved by Fritzing 0.9.3b)
breadboards: 1

parts:
  IR1 = TSOP312.., 314.. [package=THT]
  Part1 = Arduino Uno (Rev3)
  LED1 = LED - 5mm [color="Red (633nm)" package="5 mm [THT]"]
  R1 = Resistor [tolerance=±5% resistance=1k package=THT]
  LED2 = LED - 5mm [color="Red (633nm)" package="5 mm [THT]"]
  R2 = Resistor [tolerance=±5% resistance=1k package=THT]
  LED3 = LED - 5mm [color="Red (633nm)" package="5 mm [THT]"]
  R3 = Resistor [tolerance=±5% resistance=1k package=THT]

nets:
  GND: IR1.GND, Part1.GND, LED1.cathode, LED2.cathode, LED3.cathode
  N1: IR1.Vs, Part1.5V
  N2: IR1.Data, Part1.D11_PWM/MOSI
  N3: Part1.D2, R1.Pin_0
  N4: Part1.D3_PWM, R3.Pin_0
  N5: Part1.D4, R2.Pin_0
  N6: LED1.anode, R1.Pin_1
  N7: LED2.anode, R2.Pin_1
  N8: LED3.anode, R3.Pin_1
