# Fritzing sketch IRDemo (saved by Fritzing 0.9.3b)
breadboards: 1

parts:
  LED1 = LED - 5mm [color="White (4500K)" package="5 mm [THT]"]
  LED2 = LED - 5mm [color="Infrared (940nm)" package="5 mm [THT]"]
  LED3 = LED - 5mm [color="Red (633nm)" package="5 mm [THT]"]
  R1 = Resistor [tolerance=±5% resistance=2.7k package=THT]
  R2 = Resistor [tolerance=±5% resistance=150 package=THT]
  R3 = Resistor [tolerance=±5% resistance=33k package=THT]
  Part1 = Arduino Uno (Rev3)

nets:
  N1: LED1.cathode, LED2.cathode, LED3.cathode, Part1.GND
  N2: LED1.anode, R2.Pin_1
  N3: LED2.anode, R1.Pin_1, Part1.A0
  N4: LED3.anode, R3.Pin_1
  N5: R1.Pin_0, Part1.D2
  N6: R2.Pin_0, Part1.5V
  N7: R3.Pin_0, Part1.D13/SCK
