# Fritzing sketch Ard-LCD-DHT (saved by Fritzing 0.9.2b)
breadboards: 1

parts:
  Part1 = Arduino Uno (Rev3)
  LCD1 = LCD screen
  U1 = POT [package=pot_mammoth]
  DHT1 = DHT22 Humidity and Temperature Sensor
  R1 = Resistor [tolerance=±5% resistance=4.7k package=THT]

nets:
  N1: Part1.D8, LCD1.E
  N2: Part1.D9_PWM, LCD1.DB4
  N3: Part1.D10_PWM/SS, LCD1.DB5
  N4: Part1.D11_PWM/MOSI, LCD1.DB6
  N5: Part1.D12/MISO, LCD1.DB7
  N6: Part1.D2, DHT1.DATA, R1.Pin_1
  N7: Part1.D7, LCD1.RS
  VDD: Part1.5V, LCD1.VDD, LCD1.LED+, U1.S, DHT1.VDD, R1.Pin_0
  GND: Part1.GND, LCD1.VSS, LCD1.R/W, LCD1.LED-, U1.E, DHT1.GND
  N8: LCD1.V0, U1.A
