# Fritzing sketch ArduinoProgramming (saved by Fritzing 0.9.2b)
breadboards: 1

parts:
  LED1 = LED - 5mm [color="Red (633nm)" package="5 mm [THT]"]
  LED2 = LED - 5mm [color="Red (633nm)" package="5 mm [THT]"]
  LED3 = LED - 5mm [color="Red (633nm)" package="5 mm [THT]"]
  LED4 = LED - 5mm [color="Red (633nm)" package="5 mm [THT]"]
  S1 = Pushbutton [package="[THT]"]
  R1 = Resistor [tolerance=±5% resistance=10k package=THT]
  R2 = Resistor [tolerance=±5% resistance=1k package=THT]
  R3 = Resistor [tolerance=±5% resistance=1k package=THT]
  R4 = Resistor [tolerance=±5% resistance=1k package=THT]
  R5 = Resistor [tolerance=±5% resistance=1k package=THT]
  part = Arduino Uno (Rev3)

nets:
  N1: LED1.cathode, R2.Pin_1
  N2: LED1.anode, part.D13/SCK
  N3: LED2.cathode, R3.Pin_1
  N4: LED2.anode, part.D12/MISO
  N5: LED3.cathode, R4.Pin_1
  N6: LED3.anode, part.D11_PWM/MOSI
  N7: LED4.cathode, R5.Pin_1
  N8: LED4.anode, part.D10_PWM/SS
  N9: S1.Pin_1, S1.Pin_2, R2.Pin_0, R3.Pin_0, R4.Pin_0, R5.Pin_0, part.GND
  N10: S1.Pin_3, S1.Pin_4, R1.Pin_1, part.D2
  N11: R1.Pin_0, part.5V
