# Fritzing sketch SensorEyes (saved by Fritzing 0.9.3b)
breadboards: 1

parts:
  PIR1 = PIR sensor
  HC-SR04_Sensor_1 = HC-SR04 Ultrasonic Distance Sensor
  YwRobot_Power_Supply1 = YwRobot Breadboard Power Supply [part_number=545043]
  Part1 = Arduino Uno (Rev3)
  LED1 = LED - 5mm [color="Red (633nm)" package="5 mm [THT]"]
  LED2 = LED - 5mm [color="Red (633nm)" package="5 mm [THT]"]

nets:
  N1: PIR1.VDD, YwRobot_Power_Supply1.VCC#9, YwRobot_Power_Supply1.VCC#10
  N2: PIR1.SIG, Part1.D2
  GND: PIR1.GND, HC-SR04_Sensor_1.GND, YwRobot_Power_Supply1.GND#13, YwRobot_Power_Supply1.GND#14, Part1.GND, LED2.cathode
  N3: HC-SR04_Sensor_1.VCC, Part1.D13/SCK
  N4: HC-SR04_Sensor_1.TRIG, Part1.D12/MISO
  N5: HC-SR04_Sensor_1.ECHO, Part1.D11_PWM/MOSI
  N6: YwRobot_Power_Supply1.VCC#5, YwRobot_Power_Supply1.VCC#6
  N7: YwRobot_Power_Supply1.GND#11, YwRobot_Power_Supply1.GND#12
  N8: Part1.D3_PWM, LED1.anode
  N9: LED1.cathode, LED2.anode

custom parts:
  YwRobot Breadboard Power Supply: The YwRobot Breadboard Power Supply (MB-V2) has two power rails; they can be 5V or 3V3. Power to the module can be provided through the female USB socket or through the A10 (female) 2.1mm power jack.
