# Fritzing sketch SevenSegment-2 (saved by Fritzing 0.9.3b)
breadboards: 1

parts:
  7_Segment_4_Digit_Display1 = 7-SEGMENT-4DIGIT common anode [part_number="5461BS - 5462BS" package=7-segment-4digit-anode]
  Part1 = Arduino Uno (Rev3)
  U1 = 74HC595 [package="DIP16 [THT]"]
  R1 = Resistor [tolerance=±5% resistance=1k package=THT]
  R2 = Resistor [tolerance=±5% resistance=1k package=THT]
  R3 = Resistor [tolerance=±5% resistance=1k package=THT]
  R4 = Resistor [tolerance=±5% resistance=1k package=THT]

nets:
  N1: 7_Segment_4_Digit_Display1.pin_1, U1.Q4
  N2: 7_Segment_4_Digit_Display1.pin_2, U1.Q3
  N3: 7_Segment_4_Digit_Display1.pin_3, U1.Q7
  N4: 7_Segment_4_Digit_Display1.pin_4, U1.Q2
  N5: 7_Segment_4_Digit_Display1.pin_5, U1.Q6
  N6: 7_Segment_4_Digit_Display1.pin_6, R4.Pin_0
  N7: 7_Segment_4_Digit_Display1.pin_7, U1.Q1
  N8: 7_Segment_4_Digit_Display1.pin_8, R3.Pin_0
  N9: 7_Segment_4_Digit_Display1.pin_9, R2.Pin_0
  N10: 7_Segment_4_Digit_Display1.pin_10, U1.Q5
  N11: 7_Segment_4_Digit_Display1.pin_11, U1.Q0
  N12: 7_Segment_4_Digit_Display1.pin_12, R1.Pin_1
  N13: Part1.D9_PWM, R4.Pin_1
  N14: Part1.D10_PWM/SS, R3.Pin_1
  N15: Part1.D11_PWM/MOSI, R2.Pin_1
  N16: Part1.D12/MISO, R1.Pin_0
  N17: Part1.D4, U1.DS
  N18: Part1.D5_PWM, U1.ST_CP
  N19: Part1.D6_PWM, U1.SH_CP
  5V: Part1.5V, U1.MR, U1.VCC
  GND: Part1.GND, U1.GND, U1.OE

custom parts:
  7-SEGMENT-4DIGIT common anode: A 7 Segment 4 Digit common anode display, with decimal points
