# Fritzing sketch ShiftReg (saved by Fritzing 0.9.3b)
breadboards: 1

parts:
  U1 = 74HC595 [package="DIP16 [THT]"]
  R1 = Resistor [tolerance=±5% resistance=220 package=THT]
  R2 = Resistor [tolerance=±5% resistance=220 package=THT]
  R3 = Resistor [tolerance=±5% resistance=220 package=THT]
  R4 = Resistor [tolerance=±5% resistance=220 package=THT]
  R5 = Resistor [tolerance=±5% resistance=220 package=THT]
  R6 = Resistor [tolerance=±5% resistance=220 package=THT]
  R7 = Resistor [tolerance=±5% resistance=220 package=THT]
  R8 = Resistor [tolerance=±5% resistance=220 package=THT]
  LED1 = LED - 5mm [color="Red (633nm)" package="5 mm [THT]"]
  LED2 = LED - 5mm [color="Red (633nm)" package="5 mm [THT]"]
  LED3 = LED - 5mm [color="Red (633nm)" package="5 mm [THT]"]
  LED4 = LED - 5mm [color="Red (633nm)" package="5 mm [THT]"]
  LED5 = LED - 5mm [color="Blue (430nm)" package="5 mm [THT]"]
  LED6 = LED - 5mm [color="Blue (430nm)" package="5 mm [THT]"]
  LED7 = LED - 5mm [color="Blue (430nm)" package="5 mm [THT]"]
  LED8 = LED - 5mm [color="Blue (430nm)" package="5 mm [THT]"]
  Part1 = Arduino Uno (Rev3)

nets:
  N1: U1.Q1, LED6.anode
  N2: U1.Q2, LED2.anode
  N3: U1.Q3, LED5.anode
  N4: U1.Q4, LED3.anode
  N5: U1.Q5, LED7.anode
  N6: U1.Q6, LED4.anode
  N7: U1.Q7, LED8.anode
  GND: U1.GND, U1.OE, R1.Pin_0, R2.Pin_0, R3.Pin_0, R4.Pin_0, R5.Pin_0, R6.Pin_0, R7.Pin_0, R8.Pin_0, Part1.GND
  VCC: U1.MR, U1.VCC, Part1.3V3
  N8: U1.SH_CP, Part1.D11_PWM/MOSI
  N9: U1.ST_CP, Part1.D12/MISO
  N10: U1.DS, Part1.D13/SCK
  N11: U1.Q0, LED1.anode
  N12: R1.Pin_1, LED1.cathode
  N13: R2.Pin_1, LED6.cathode
  N14: R3.Pin_1, LED2.cathode
  N15: R4.Pin_1, LED5.cathode
  N16: R5.Pin_1, LED3.cathode
  N17: R6.Pin_1, LED7.cathode
  N18: R7.Pin_1, LED4.cathode
  N19: R8.Pin_1, LED8.cathode
