# Fritzing sketch TemperatureFan-1 (saved by Fritzing 0.9.3b)
breadboards: 1

parts:
  IC1 = L293D [package=THT]
  M1 = DC Motor
  Part1 = Arduino Uno (Rev3) - ICSP
  YwRobot_Power_Supply1 = YwRobot Breadboard Power Supply [part_number=545043]
  Part2 = KY-015 Temperature & Humidity Sensor Module [package="Breakout board"]

nets:
  N1: IC1.Enable_1, Part1.D5_PWM
  N2: IC1.In_1, Part1.D4
  N3: IC1.Out_1_(_Controlled_by_Enable_1_), M1.pin_1
  N4: IC1.0V, Part1.GND, YwRobot_Power_Supply1.GND#13, YwRobot_Power_Supply1.GND#14, Part2.-
  N5: IC1.Out_2_(_Controlled_by_Enable_1_), M1.pin_2
  N6: IC1.In_2, Part1.D3_PWM
  N7: IC1.+Vmotor, YwRobot_Power_Supply1.VCC#9, YwRobot_Power_Supply1.VCC#10, Part2.Vin
  N8: Part1.D2, Part2.S
  N9: YwRobot_Power_Supply1.VCC#5, YwRobot_Power_Supply1.VCC#6
  N10: YwRobot_Power_Supply1.GND#11, YwRobot_Power_Supply1.GND#12

custom parts:
  YwRobot Breadboard Power Supply: The YwRobot Breadboard Power Supply (MB-V2) has two power rails; they can be 5V or 3V3. Power to the module can be provided through the female USB socket or through the A10 (female) 2.1mm power jack.
  KY-015 Temperature & Humidity Sensor Module: DH-11 temperature and humidity sensor in KEYES KY-015 module, provides a low-latency serial interface to measure humidity and temperature.
