# Fritzing sketch touch_sensor (saved by Fritzing 0.9.2b)
breadboards: 1

parts:
  Q1 = NPN-Transistor [package="TO92 [THT]"]
  Q2 = NPN-Transistor [package="TO92 [THT]"]
  LED1 = LED - 5mm [color="Red (633nm)" package="5 mm [THT]"]
  R1 = Resistor [tolerance=±5% resistance=1k package=THT]
  Part1 = Arduino Uno (Rev3)

nets:
  N1: Q1.E, Part1.A1
  N2: Q1.B, Q2.E
  N3: Q1.C, Q2.C, Part1.5V
  N4: LED1.cathode, Part1.GND
  N5: LED1.anode, R1.Pin_0
  N6: R1.Pin_1, Part1.D3_PWM
