# Fritzing sketch ESP-096TFT (saved by Fritzing 0.9.3b)
breadboards: 1

parts:
  M1 = DOIT Esp32 DevKit v1 (30 pins long, 11 pins width) [part_number=ESP32S-PIN30]
  Part1 = Adafruit Mini TFT Display - 0.96in 160x80 [part_number="Adafruit 3533"]

nets:
  3V3: M1.3V3, Part1.VIN
  GND: M1.GND, Part1.GND
  N1: M1.D2, Part1.DC
  N2: M1.D4, Part1.TFTRST
  N3: M1.D5, Part1.TFTCS
  N4: M1.D18, Part1.SCK
  N5: M1.D23, Part1.MOSI
  N6: M1.VIN, Part1.BACKLIGHT

custom parts:
  DOIT Esp32 DevKit v1 (30 pins long, 11 pins width): The DOIT Esp32 DevKit v1 is one of the development board created by DOIT to evaluate the ESP-WROOM-32 module. It is based on the ESP32 microcontroller that boasts Wifi, Bluetooth, Ethernet and Low Power support all in a single chip. (vanepp) made breadboard work, adjusted pin numbering and labels and reduced size of schematic and cleaned up pcb. This chip is 30pins long (2 x15) and 11 pins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
  Adafruit Mini TFT Display - 0.96in 160x80: It's the size of your thumbnail, with glorious 160x80 pixel color... it's the Adafruit Mini TFT Breakout! This very very small display is only 0.96" diagonal, packed with RGB pixels, for making very small high-density displays. The display uses 4-wire SPI to communicate and has its own pixel-addressable frame buffer, it can be used with every kind of microcontroller. Even a very small one with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
