# Fritzing sketch ESP-TFT_Wiring (saved by Fritzing 0.9.3b)

parts:
  U1 = NodeMCU V1.0
  Part1 = Adafruit 1.8 inch TFT Shield [part_number="Adafruit #802"]

nets:
  N1: U1.D4, Part1.D9
  3V3: U1.3V3, Part1.+5V
  GND: U1.GND, Part1.GND
  N2: U1.D5, Part1.SCK
  N3: U1.D7, Part1.MOSI
  N4: U1.D8, Part1.TFT_CS
  N5: U1.RST, Part1.RESET

custom parts:
  NodeMCU V1.0: ESP8266 based NodeMCU
  Adafruit 1.8 inch TFT Shield: This lovely little shield is the best way to add a small, colorful and bright display to any project. We took our popular 1.8" TFT breakout board and remixed it into an Arduino shield complete with microSD card slot and a 5-way joystick navigation switch (with a nice plastic knob)! Since the display uses only 4 pins to communicate and has its own pixel-addressable frame buffer, it can be used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
