# Fritzing sketch ESP-Webservices (saved by Fritzing 0.9.3b)
breadboards: 1

parts:
  LCD1 = LCD screen
  M1 = DOIT Esp32 DevKit v1 (30 pins long, 11 pins width) [part_number=ESP32S-PIN30]
  R1 = Rotary Potentiometer (Small) [maximum_resistance=100kΩ package=THT]

nets:
  VSS: LCD1.VSS, LCD1.R/W, LCD1.LED-, M1.GND, R1.leg1
  VDD: LCD1.VDD, LCD1.LED+, M1.VIN
  N1: LCD1.V0, R1.wiper
  N2: LCD1.RS, M1.D5
  N3: LCD1.E, M1.D18
  N4: LCD1.DB4, M1.D19
  N5: LCD1.DB5, M1.D21
  N6: LCD1.DB6, M1.D22
  N7: LCD1.DB7, M1.D23
  N8: M1.3V3, R1.leg2

custom parts:
  DOIT Esp32 DevKit v1 (30 pins long, 11 pins width): The DOIT Esp32 DevKit v1 is one of the development board created by DOIT to evaluate the ESP-WROOM-32 module. It is based on the ESP32 microcontroller that boasts Wifi, Bluetooth, Ethernet and Low Power support all in a single chip. (vanepp) made breadboard work, adjusted pin numbering and labels and reduced size of schematic and cleaned up pcb. This chip is 30pins long (2 x15) and 11 pins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
