# Fritzing sketch IR_Receive (saved by Fritzing 0.9.3b)
breadboards: 1

parts:
  YwRobot_Power_Supply1 = YwRobot Breadboard Power Supply [part_number=545043]
  Part1 = KY-022 Infrared Receiver Module [package="Breakout board"]
  R1 = Resistor [tolerance=±5% resistance=220 package=THT]
  LED1 = LED - 5mm [color="Blue (470nm)" package="5 mm [THT]"]

nets:
  N1: YwRobot_Power_Supply1.VCC#5, YwRobot_Power_Supply1.VCC#6, Part1.Vin, LED1.anode
  N2: YwRobot_Power_Supply1.VCC#9, YwRobot_Power_Supply1.VCC#10
  N3: YwRobot_Power_Supply1.GND#11, YwRobot_Power_Supply1.GND#12, Part1.-
  N4: YwRobot_Power_Supply1.GND#13, YwRobot_Power_Supply1.GND#14
  N5: Part1.S, R1.Pin_0
  N6: R1.Pin_1, LED1.cathode

custom parts:
  YwRobot Breadboard Power Supply: The YwRobot Breadboard Power Supply (MB-V2) has two power rails; they can be 5V or 3V3. Power to the module can be provided through the female USB socket or through the A10 (female) 2.1mm power jack.
  KY-022 Infrared Receiver Module: Arduino IR receiver module KY-022, based on 1838 IR Receiver/Decoder. It reacts to 38kHz infrared light.
