# Fritzing sketch IR_Send_ESP32 (saved by Fritzing 0.9.3b)
breadboards: 1

parts:
  M1 = DOIT Esp32 DevKit v1 (30 pins long, 11 pins width) [part_number=ESP32S-PIN30]
  YwRobot_Power_Supply1 = YwRobot Breadboard Power Supply [part_number=545043]
  R1 = Resistor [tolerance=±5% resistance=470 package=THT]
  LED1 = LED - 5mm [color="Infrared (850nm)" package="5 mm [THT]"]
  Q1 = TRANSISTOR_NPN [package=to-92]

nets:
  N1: M1.GND, YwRobot_Power_Supply1.GND#13, YwRobot_Power_Supply1.GND#14, Q1.E
  N2: M1.D4, R1.Pin_1
  N3: YwRobot_Power_Supply1.VCC#5, YwRobot_Power_Supply1.VCC#6
  N4: YwRobot_Power_Supply1.VCC#9, YwRobot_Power_Supply1.VCC#10, LED1.anode
  N5: YwRobot_Power_Supply1.GND#11, YwRobot_Power_Supply1.GND#12
  N6: R1.Pin_0, Q1.B
  N7: LED1.cathode, Q1.C

custom parts:
  DOIT Esp32 DevKit v1 (30 pins long, 11 pins width): The DOIT Esp32 DevKit v1 is one of the development board created by DOIT to evaluate the ESP-WROOM-32 module. It is based on the ESP32 microcontroller that boasts Wifi, Bluetooth, Ethernet and Low Power support all in a single chip. (vanepp) made breadboard work, adjusted pin numbering and labels and reduced size of schematic and cleaned up pcb. This chip is 30pins long (2 x15) and 11 pins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
  YwRobot Breadboard Power Supply: The YwRobot Breadboard Power Supply (MB-V2) has two power rails; they can be 5V or 3V3. Power to the module can be provided through the female USB socket or through the A10 (female) 2.1mm power jack.
