# Fritzing sketch 555-Timer (saved by Fritzing 0.9.2b)
circuit board: 4.99079cm x 3.91801cm
breadboards: 1

parts:
  U1 = 555 Timer [package="DIP8 [THT]"]
  C1 = Electrolytic Capacitor [capacitance=1µF package="100 mil [THT, electrolytic]"]
  R2 = Resistor [tolerance=±5% resistance=470k package=THT]
  R1 = Resistor [tolerance=±5% resistance=1k package=THT]
  R3 = Resistor [tolerance=±5% resistance=1k package=THT]
  LED1 = LED - 5mm [color="Green (570nm)" package="5 mm [THT]"]

nets:
  GND: U1.Ground, C1.-, LED1.cathode
  N1: U1.Trigger, U1.Threshold, C1.+, R2.Pin_0
  N2: U1.Output, R3.Pin_0
  9V: U1.Reset, U1.Vcc_Supply_Voltage, R1.Pin_0
  N3: U1.Discharge, R2.Pin_1, R1.Pin_1
  N4: R3.Pin_1, LED1.anode
