# Fritzing sketch DarlingtonPair (saved by Fritzing 0.9.2b)
circuit board: 8.46667cm x 5.64444cm
breadboards: 1

parts:
  Q1 = NPN-Transistor [package="TO92 [THT]"]
  Q2 = NPN-Transistor [package="TO92 [THT]"]
  LED1 = LED - 5mm [color="Green (570nm)" package="5 mm [THT]"]
  VCC1 = 4 x AAA Battery Mount

nets:
  N1: Q1.E, Q2.B
  N2: Q1.C, Q2.C, LED1.cathode
  N3: Q2.E, VCC1.-
  N4: LED1.anode, VCC1.+
