# Fritzing sketch flashing_light (saved by Fritzing 0.9.2b)
circuit board: 3.35501cm x 3.17537cm
breadboards: 1

parts:
  Q1 = NPN-Transistor [package="TO92 [THT]"]
  R1 = Resistor [tolerance=±5% resistance=470k package=THT]
  R2 = Resistor [tolerance=±5% resistance=1k package=THT]
  R3 = Resistor [tolerance=±5% resistance=100k package=THT]
  C1 = Electrolytic Capacitor [capacitance=4.7µF voltage=50V package="100 mil [THT, electrolytic]"]
  LED1 = LED - 5mm [color="Red (633nm)" package="5 mm [THT]"]
  R4 = Resistor [tolerance=±5% resistance=220 package=THT]
  Q2 = PNP-Transistor [package="TO92 [THT]"]
  VCC1 = Battery

nets:
  N1: Q1.E, R3.Pin_0, C1.-, VCC1.-
  N2: Q1.B, Q2.C
  N3: Q1.C, LED1.cathode
  N4: R1.Pin_0, R2.Pin_0, C1.+
  N5: R1.Pin_1, R4.Pin_1, VCC1.+
  N6: R2.Pin_1, Q2.E
  N7: R3.Pin_1, Q2.B
  N8: LED1.anode, R4.Pin_0
