# Fritzing sketch MOSFET-1 (saved by Fritzing 0.9.3b)
breadboards: 1

parts:
  Q1 = Basic FET N-Channel [package="TO220 [THT]"]
  Part1 = Arduino Uno (Rev3)
  VCC1 = Battery block 9V
  M1 = DC Motor

nets:
  N1: Q1.gate, Part1.D3_PWM
  N2: Q1.drain, M1.pin_2
  N3: Q1.source, Part1.GND, VCC1.-
  N4: VCC1.+, M1.pin_1
