# Fritzing sketch MOSFET-2 (saved by Fritzing 0.9.3b)
breadboards: 1

parts:
  Q1 = Basic FET N-Channel [package="TO220 [THT]"]
  Part1 = Arduino Uno (Rev3)
  VCC1 = Battery block 9V
  M1 = DC Motor
  R1 = Rotary Potentiometer (Small) [maximum_resistance=10kΩ package=THT]
  R2 = Resistor [tolerance=±5% resistance=1k package=THT]

nets:
  N1: Q1.gate, Part1.D3_PWM
  N2: Q1.drain, M1.pin_2
  N3: Q1.source, Part1.GND, VCC1.-, R1.leg2
  N4: Part1.A0, R1.wiper, R2.Pin_1
  N5: Part1.5V, R1.leg1, R2.Pin_0
  N6: VCC1.+, M1.pin_1
