# Fritzing sketch ManualLCD-8 (saved by Fritzing 0.9.3b)
breadboards: 1

parts:
  S1 = Toggle Switch [package=THT]
  S2 = Toggle Switch [package=THT]
  S3 = Toggle Switch [package=THT]
  S4 = Toggle Switch [package=THT]
  S5 = Toggle Switch [package=THT]
  S6 = Toggle Switch [package=THT]
  S7 = Toggle Switch [package=THT]
  S8 = Toggle Switch [package=THT]
  S9 = Toggle Switch [package=THT]
  R1 = Resistor [tolerance=±5% resistance=1k package=THT]
  LCD1 = LCD screen
  S11 = Pushbutton [package=THT]
  R2 = Rotary Potentiometer (Small) [maximum_resistance=100kΩ package=THT]

nets:
  N1: S1.L1, S2.L1, S3.L1, S4.L1, S5.L1, S6.L1, S7.L1, S8.L1, S9.L1, R1.Pin_1, LCD1.VSS, LCD1.R/W, R2.leg1
  N2: S1.COM, LCD1.DB0
  N3: S1.L2, S2.L2, S3.L2, S4.L2, S5.L2, S6.L2, S7.L2, S8.L2, S9.L2, LCD1.VDD, S11.leg1, R2.leg2
  N4: S2.COM, LCD1.DB1
  N5: S3.COM, LCD1.DB2
  N6: S4.COM, LCD1.DB3
  N7: S5.COM, LCD1.DB4
  N8: S6.COM, LCD1.DB5
  N9: S7.COM, LCD1.DB6
  N10: S8.COM, LCD1.DB7
  N11: S9.COM, LCD1.RS
  N12: R1.Pin_0, LCD1.E, S11.leg0
  N13: LCD1.V0, R2.wiper
