# Fritzing sketch trans-switch (saved by Fritzing 0.9.2b)
breadboards: 1

parts:
  Q1 = NPN-Transistor [package="TO92 [THT]"]
  R1 = Resistor [tolerance=±5% resistance=1k package=THT]
  LED1 = LED - 5mm [color="Blue (470nm)" package="5 mm [THT]"]
  VCC1 = Battery
  S1 = Pushbutton [package=THT]

nets:
  N1: Q1.E, VCC1.-
  N2: Q1.B, R1.Pin_0
  N3: Q1.C, LED1.cathode
  N4: R1.Pin_1, S1.leg0
  N5: LED1.anode, VCC1.+, S1.leg1
