# Fritzing sketch RemoteTemp (saved by Fritzing 0.9.3b)
breadboards: 1

parts:
  U1 = NodeMCU V1.0
  Part2 = Adafruit 1.8 inch TFT Shield [part_number="Adafruit #802"]
  DHT1 = DHT22 Humidity and Temperature Sensor

nets:
  N1: U1.D2, DHT1.DATA
  N2: U1.D3, Part2.TFT_DC
  N3: U1.D4, Part2.D9
  3V3: U1.3V3, Part2.+5V, DHT1.VDD
  GND: U1.GND, Part2.GND, DHT1.GND
  N4: U1.D5, Part2.SCK
  N5: U1.D7, Part2.MOSI
  N6: U1.D8, Part2.TFT_CS

custom parts:
  NodeMCU V1.0: ESP8266 based NodeMCU
  Adafruit 1.8 inch TFT Shield: This lovely little shield is the best way to add a small, colorful and bright display to any project. We took our popular 1.8" TFT breakout board and remixed it into an Arduino shield complete with microSD card slot and a 5-way joystick navigation switch (with a nice plastic knob)! Since the display uses only 4 pins to communicate and has its own pixel-addressable frame buffer, it can be used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
