# Fritzing sketch RPi-Analog (saved by Fritzing 0.9.2b)
breadboards: 1

parts:
  Raspberry_Pi1 = Raspberry Pi 2
  IC1 = IC, DIP package, 16 pins [chip_label=MCP3008-I/P]
  R1 = Rotary Potentiometer (Large) [maximum_resistance=100kΩ package=THT]
  LED1 = LED - 5mm [color="Blue (470nm)" package="5 mm [THT]"]
  R2 = Resistor [tolerance=±5% resistance=1k package=THT]

nets:
  3V3: Raspberry_Pi1.3v3, Raspberry_Pi1.3V3, IC1.pin15, IC1.pin16, R1.leg2
  N1: Raspberry_Pi1.GPIO22, IC1.pin13
  N2: Raspberry_Pi1.GPIO25, IC1.pin10
  N3: Raspberry_Pi1.GPIO24, IC1.pin11
  N4: Raspberry_Pi1.GPIO23, IC1.pin12
  N5: Raspberry_Pi1.GPIO18, LED1.anode
  N6: Raspberry_Pi1.GND, IC1.pin9, IC1.pin14, R1.leg1, R2.Pin_1
  N7: IC1.pin1, R1.wiper
  N8: LED1.cathode, R2.Pin_0
