# Fritzing sketch Character Display (saved by Fritzing 0.9.2b)
breadboards: 1

parts:
  LCD1 = LCD screen
  J2 = Cobbler Plus
  U1 = POT [package=pot_mammoth]

nets:
  N1: LCD1.VSS, LCD1.R/W, LCD1.LED+, J2.SCL, U1.E
  N2: LCD1.VDD, LCD1.LED-, J2.MISO, U1.S
  N3: LCD1.V0, U1.A
  N4: LCD1.RS, J2.#5
  N5: LCD1.E, J2.#6
  N6: LCD1.DB4, J2.5.0V#3
  N7: LCD1.DB5, J2.#22
  N8: LCD1.DB6, J2.#23
  N9: LCD1.DB7, J2.3.3V

custom parts:
  Cobbler Plus: The Cobbler Plus is an add on prototyping board from Adafruit specifically designed for the Raspberry Pi B+ that can break out all those tasty power, GPIO, I2C and SPI pins from the 40-pin header onto a solderless breadboard. This set will make "cobbling together" prototypes with the Pi super easy. The Cobbler Plus can plug into any solderless breadboard.
